# Fritzing sketch bit_banging (saved by Fritzing 0.9.3b)
breadboards: 1

parts:
  Part1 = Arduino Nano (Rev3.0)
  Part3 = Bluetooth HC-05 Macho

nets:
  USB: Part1.D1/TX, Part1.D0/RX
  GND: Part1.GND, Part3.GND
  N1: Part1.D7, Part3.State
  N2: Part1.D8, Part3.TXD
  N3: Part1.D9, Part3.RXD
  5V: Part1.5V, Part3.VCC
