# Fritzing sketch ir_sensor (saved by Fritzing 0.9.3b)
breadboards: 1

parts:
  Part1 = Arduino Nano (Rev3.0)
  J1 = Infrared Proximity Sensor

nets:
  GND: Part1.GND, J1.GND
  5V: Part1.5V, J1.Vcc
  N1: Part1.A0, J1.Vout
