# Fritzing sketch lcd (saved by Fritzing 0.9.3b)
breadboards: 1

parts:
  part = Arduino Nano (Rev3.0)
  LCD1 = LCD screen
  R1 = Trimmer Potentiometer [package=THT]

nets:
  N1: part.D2, LCD1.DB7
  N2: part.D3, LCD1.DB6
  N3: part.D4, LCD1.DB5
  N4: part.D5, LCD1.DB4
  N5: part.D11/MOSI, LCD1.E
  N6: part.D12/MISO, LCD1.RS
  GND: part.GND, LCD1.VSS, R1.leg1
  5V: part.5V, LCD1.VDD, R1.leg2
  N7: LCD1.V0, R1.wiper
