# Fritzing sketch mosfet_as_switch (saved by Fritzing 0.9.3b)
breadboards: 1

parts:
  part = Arduino Nano (Rev3.0)
  Q2 = MOSFET-NCHANNEL [package=to220v]
  M1 = DC Motor
  VCC1 = Battery block 9V

nets:
  N1: part.D6, Q2.G
  N2: part.GND, Q2.S, VCC1.-
  N3: Q2.D, M1.pin_2
  N4: M1.pin_1, VCC1.+
