# Fritzing sketch pull_up (saved by Fritzing 0.9.3b)
breadboards: 1

parts:
  part = Arduino Nano (Rev3.0)
  R1 = Resistor [tolerance=±5% resistance=10k package=THT]
  S2 = Pushbutton [package=THT]

nets:
  N1: part.GND, S2.leg0
  N2: part.D3, R1.Pin_1, S2.leg1
  N3: part.3V3, R1.Pin_0
