# Fritzing sketch whackamole (saved by Fritzing 0.9.3b)
breadboards: 1

parts:
  Part1 = Arduino Nano (Rev3.0)
  R1 = Resistor [tolerance=±5% resistance=330 package=THT]
  R2 = Resistor [tolerance=±5% resistance=330 package=THT]
  R3 = Resistor [tolerance=±5% resistance=330 package=THT]
  R4 = Resistor [tolerance=±5% resistance=330 package=THT]
  LED1 = LED - 5mm [color="Red (633nm)" package="5 mm [THT]"]
  LED2 = LED - 5mm [color="Red (633nm)" package="5 mm [THT]"]
  LED3 = LED - 5mm [color="Red (633nm)" package="5 mm [THT]"]
  LED4 = LED - 5mm [color="Red (633nm)" package="5 mm [THT]"]
  S1 = Pushbutton [package=THT]
  R5 = Resistor [tolerance=±5% resistance=10k package=THT]
  R6 = Resistor [tolerance=±5% resistance=330 package=THT]
  LED5 = LED - 5mm [color="Red (633nm)" package="5 mm [THT]"]

nets:
  N1: Part1.GND, LED1.cathode, LED2.cathode, LED3.cathode, LED4.cathode, R5.Pin_1, LED5.cathode
  N2: Part1.D2, S1.leg1, R5.Pin_0
  N3: Part1.D5, R1.Pin_0
  N4: Part1.D6, R2.Pin_0
  N5: Part1.D10, R4.Pin_0
  N6: Part1.D11/MOSI, R3.Pin_0
  N7: Part1.D12/MISO, R6.Pin_0
  N8: Part1.5V, S1.leg0
  N9: R1.Pin_1, LED4.anode
  N10: R2.Pin_1, LED3.anode
  N11: R3.Pin_1, LED1.anode
  N12: R4.Pin_1, LED2.anode
  N13: R6.Pin_1, LED5.anode
